// Logisim project cpu.circ as structural Verilog: 1 circuit, main circuit cpu
module cpu (
  input  clk,
  input  [31:0] Instruction,
  input  [31:0] MemReadData,
  output [31:0] MemAddress,
  output [31:0] ProgramCounter,
  output [31:0] ra,
  output [31:0] sp,
  output [31:0] t0,
  output [31:0] t1,
  output [31:0] t2,
  output [31:0] s0,
  output [31:0] s1,
  output [31:0] a0,
  output [3:0] MemWriteMask,
  output [31:0] MemWriteData
);

  wire AS, BS, BU, control_logic_1_pcsel, MWE, RWE;
  wire [1:0] WBS;
  wire [2:0] IMMS;
  wire [3:0] control_logic_1_alusel;
  wire [31:0] alu_1_aluresult, IMM, multiplexer_1_out, multiplexer_2_out, multiplexer_3_out, PCFOUR, RD1,
       RD2, undriven;

  Register #(.width(32)) PC (.D(PCFOUR), .en(1'b1), .clk(clk), .Q(ProgramCounter));  // open: clr
  Adder #(.width(32)) adder_1 (.a(ProgramCounter), .b(32'h4), .out(PCFOUR));  // open: cin, cout
  control_logic control_logic_1 (
    .Instruction(Instruction), .PCSel(control_logic_1_pcsel), .RegWEn(RWE), .ImmSel(IMMS), .BrUn(BU),
    .ASel(AS), .BSel(BS), .ALUSel(control_logic_1_alusel), .MemWEn(MWE), .WBSel(WBS));  // open: BrEq, BrLt
  regfile regfile_1 (
    .ReadIndex1(Instruction[19:15]), .ReadIndex2(Instruction[24:20]), .WriteIndex(Instruction[11:7]),
    .WriteData(multiplexer_3_out), .RegWEn(RWE), .clk(clk), .ra(ra), .sp(sp), .t0(t0), .t1(t1), .t2(t2),
    .s0(s0), .s1(s1), .a0(a0), .ReadData1(RD1), .ReadData2(RD2));
  imm_gen imm_gen_1 (.Instruction(Instruction), .ImmSel(IMMS), .Immediate(IMM));
  Multiplexer #(.width(32)) multiplexer_1 (.in0(RD1), .in1(ProgramCounter), .out(multiplexer_1_out), .sel(AS));
  Multiplexer #(.width(32)) multiplexer_2 (.in0(RD2), .in1(IMM), .out(multiplexer_2_out), .sel(BS));
  alu alu_1 (
    .A(multiplexer_1_out), .B(multiplexer_2_out), .ALUSel(control_logic_1_alusel), .ALUResult(alu_1_aluresult));
  Multiplexer #(.select(2), .width(32)) multiplexer_3 (
    .in0(undriven), .in1(alu_1_aluresult), .in2(PCFOUR), .out(multiplexer_3_out), .sel(WBS));  // open: in3
  branch_comp branch_comp_1 (.BrUn(BU));  // open: BrData1, BrData2, BrEq, BrLt
  partial_store partial_store_1 (.MemWEn(MWE));  // open: Instruction, MemAddress, DataFromReg, MemWriteMask, DataToMem
  // partial_load partial_load_1: pin names not known

  // Other names for the same wires on the sheet: OPC[6:0] = Instruction[6:0]; RD[4:0] = Instruction[11:7];
  //   F3[2:0] = Instruction[14:12]; RI1[4:0] = Instruction[19:15]; RI2[4:0] = Instruction[24:20];
  //   F7[6:0] = Instruction[31:25]

  // Notes on the sheet:
  //   To IMEM
  //   IMEM (do **NOT** move this)
  //   From IMEM
  //   Inputs/Outputs for testing. Do **NOT** move these.
  //   It is OK to move the PC, RegFile, ALU, MEM, Branch Comp, Imm Gen, Partial Load, Partial Store and Control Logic to wherever is most convenient for you when constructing your CPU, and to delete this text
  //   To DMEM
  //   DMEM (do **NOT** move this)
  //   From DMEM
endmodule
