// Logisim project partial-store.circ as structural Verilog: 1 circuit, main circuit partial_store
module partial_store (
  input  [31:0] Instruction,
  input  [31:0] MemAddress,
  input  [31:0] DataFromReg,
  input  MemWEn,
  output [3:0] MemWriteMask,
  output [31:0] DataToMem
);

  wire [31:0] bit_extender_1_out, bit_extender_2_out, bit_extender_3_out, DataToStore, multiplexer_1_out,
       multiplexer_2_out, undriven;

  assign bit_extender_1_out = {{16{1'b0}}, DataFromReg[15:0]};  // Bit_Extender bit_extender_1
  assign bit_extender_2_out = {{16{1'b0}}, DataFromReg[15:0]};  // Bit_Extender bit_extender_2
  assign bit_extender_3_out = {{24{1'b0}}, DataFromReg[7:0]};  // Bit_Extender bit_extender_3
  Multiplexer #(.select(2), .width(32)) multiplexer_1 (
    .in0(bit_extender_2_out), .in2({bit_extender_1_out[15:0], bit_extender_1_out[31:16]}),
    .out(multiplexer_1_out), .sel(MemAddress[1:0]));  // open: in1, in3
  Multiplexer #(.select(2), .width(32)) multiplexer_2 (
    .in0(bit_extender_3_out), .in1(undriven), .out(multiplexer_2_out), .sel(MemAddress[1:0]));  // open: in2, in3
  Multiplexer #(.select(2), .width(32)) multiplexer_3 (
    .in0(multiplexer_2_out), .in1(multiplexer_1_out), .in2(DataFromReg), .out(DataToStore),
    .sel(Instruction[13:12]));  // open: in3

  // Other names for the same wires on the sheet: Bottom8[7:0] = DataFromReg[7:0]; Bottom16[15:0] = DataFromReg[15:0];
  //   Func3[1:0] = Instruction[13:12]; bottom2[1:0] = MemAddress[1:0]

  // Notes on the sheet:
  //   INPUTS to your circuit
  //   DON'T CHANGE THE LOCATIONS OF THE INPUTS AND OUTPUTS!
  //   OUTPUT from your circuit
endmodule
